# Fritzing sketch cablage (saved by Fritzing 0.9.4)
breadboards: 1

parts:
  Composant1 = Arduino Due (Rev2b)
  S2 = Pushbutton [package="[SMD]"]
  S3 = Pushbutton [package="[SMD]"]
  LED2 = LED - 3mm [color="Green (560nm)" package="3 mm [THT]"]  # not connected
  LED1 = LED - 3mm [color="Red (633nm)" package="3 mm [THT]"]
  R3 = Resistor [tolerance=±5% resistance=1k package="0805 [SMD]"]
  R4 = Resistor [tolerance=±5% resistance=1k package="0805 [SMD]"]
  R5 = Resistor [tolerance=±5% resistance=1k package="0805 [SMD]"]
  R6 = Resistor [tolerance=±5% resistance=1k package="0805 [SMD]"]
  RE1 = Rotary Encoder [package=THT]

nets:
  N1: Composant1.5V, R3.Pin_1, R4.Pin_1, R5.Pin_1, R6.Pin_1
  N2: Composant1.GND, S2.Pin_1, S2.Pin_2, S3.Pin_3, S3.Pin_4
  N3: Composant1.D4_PWM/SS1, S2.Pin_3, S2.Pin_4, R5.Pin_0
  N4: Composant1.D5_PWM, S3.Pin_1, S3.Pin_2, R4.Pin_0
  N5: Composant1.D6_PWM, LED1.cathode
  N6: Composant1.D7_PWM, R6.Pin_0
  N7: Composant1.D22, RE1.EncoderPinA
  N8: Composant1.D24, RE1.EncoderPinC
  N9: Composant1.D26, RE1.EncoderPinB
  N10: LED1.anode, R3.Pin_0
